// Logisim project inciso a.circ as structural Verilog: 1 circuit, main circuit main
module main (
  input  a,
  input  b,
  input  c,
  output x
);

  wire and_1_out, and_2_out, not_1_out;

  not not_1 (not_1_out, b);
  and and_1 (and_1_out, a, b, c);
  and and_2 (and_2_out, a, not_1_out, c);
  xor xor_1 (x, and_1_out, and_2_out);
endmodule
