// Logisim project inciso b.circ as structural Verilog: 1 circuit, main circuit main
module main (
  input  x,
  input  y,
  output F
);

  wire and_1_out, and_2_out, not_1_out;

  not not_1 (not_1_out, y);
  and and_1 (and_1_out, x, y);
  and and_2 (and_2_out, x, not_1_out);
  or or_1 (F, and_1_out, and_2_out);
endmodule
